// Logisim project toy8-halt-test-v2.circ as structural Verilog: 4 circuits, main circuit main
module main (
  input  in_1
);

  wire clock_1_out, control_1_addr_mux, control_1_halt, control_1_ir_en, control_1_pc_load, control_1_r_en,
       control_1_ram_str, not_1_out;
  wire [1:0] control_1_aluop, control_1_r_mux;
  wire [3:0] counter_1_q, multiplexer_2_out;
  wire [7:0] alu_1_out_4, bit_extender_1_out, IR_q, multiplexer_1_out, R_q, ram_1_data;

  alu alu_1 (.ALUOp(control_1_aluop), .in_2(R_q), .in_3(ram_1_data), .out_4(alu_1_out_4));
  Multiplexer #(.select(2), .width(8), .enable("false")) multiplexer_1 (
    .in0(alu_1_out_4), .in1(ram_1_data), .in2(bit_extender_1_out), .out(multiplexer_1_out),
    .sel(control_1_r_mux));  // open: in3
  assign bit_extender_1_out = {{4{1'b0}}, IR_q[3:0]};  // Bit_Extender bit_extender_1
  Register #(.trigger("falling")) R (
    .D(multiplexer_1_out), .en(control_1_r_en), .Q(R_q), .clk(clock_1_out));  // open: clr
  Register IR (.D(ram_1_data), .en(control_1_ir_en), .Q(IR_q), .clk(clock_1_out));  // open: clr
  not not_1 (not_1_out, control_1_pc_load);
  Counter #(.width(4), .max('hf), .trigger("falling")) counter_1 (
    .load(control_1_pc_load), .D(IR_q[3:0]), .count(not_1_out), .Q(counter_1_q), .clk(clock_1_out));  // open: carry, clr
  Multiplexer #(.width(4), .enable("false")) multiplexer_2 (
    .in0(counter_1_q), .in1(IR_q[3:0]), .out(multiplexer_2_out), .sel(control_1_addr_mux));
  control control_1 (
    .CLK(clock_1_out), .Opcode(IR_q[7:5]), .in_3(R_q), .halt(control_1_halt), .IR_en(control_1_ir_en),
    .R_en(control_1_r_en), .RAM_str(control_1_ram_str), .PC_load(control_1_pc_load),
    .ADDR_MUX(control_1_addr_mux), .R_MUX(control_1_r_mux), .ALUOp(control_1_aluop));
  RAM #(.addrWidth(4), .bus("separate")) ram_1 (
    .addr(multiplexer_2_out), .din(R_q), .data(ram_1_data), .str(control_1_ram_str), .clk(control_1_ram_str));  // open: sel, ld, clr
  clock clock_1 (.RUN(in_1), .HALT(control_1_halt), .OUT(clock_1_out));

  // Notes on the sheet:
  //   PC
  //   RAM
endmodule

module alu (
  input  [1:0] ALUOp,
  input  [7:0] in_2,
  input  [7:0] in_3,
  output [7:0] out_4
);

  wire [7:0] adder_1_out, and_1_out, xor_1_out;

  Adder adder_1 (.a(in_2), .b(in_3), .out(adder_1_out));  // open: cin, cout
  assign and_1_out = in_2 & in_3;  // AND_Gate and_1, 8 bits wide
  assign xor_1_out = in_2 ^ in_3;  // XOR_Gate xor_1, 8 bits wide
  Multiplexer #(.select(2), .width(8), .enable("false")) multiplexer_1 (
    .in0(adder_1_out), .in1(and_1_out), .in2(xor_1_out), .out(out_4), .sel(ALUOp));  // open: in3

  // Notes on the sheet:
  //   A
  //   B
  //   R
endmodule

module control (
  input  CLK,
  input  [2:0] Opcode,
  input  [7:0] in_3,
  output halt,
  output IR_en,
  output R_en,
  output RAM_str,
  output PC_load,
  output ADDR_MUX,
  output [1:0] R_MUX,
  output [1:0] ALUOp
);

  wire and_1_out, demultiplexer_1_out1, demultiplexer_1_out7;
  wire [7:0] not_1_out;

  assign not_1_out = ~in_3;  // NOT_Gate not_1, 8 bits wide
  Demultiplexer #(.select(3), .enable("false")) demultiplexer_1 (
    .out0(halt), .out1(demultiplexer_1_out1), .out2(ALUOp[0]), .out3(ALUOp[1]), .out4(R_MUX[1]),
    .out5(R_MUX[0]), .out6(RAM_str), .out7(demultiplexer_1_out7), .in(CLK), .sel(Opcode));
  and and_1 (and_1_out, not_1_out[0], not_1_out[1], not_1_out[2], not_1_out[3], not_1_out[4], not_1_out[5], not_1_out[6], not_1_out[7]);
  or or_1 (R_en, demultiplexer_1_out1, ALUOp[0], ALUOp[1], R_MUX[1], R_MUX[0]);
  and and_2 (PC_load, demultiplexer_1_out7, and_1_out);
  not not_2 (IR_en, CLK);

  assign ADDR_MUX = CLK;

  // Notes on the sheet:
  //   R
endmodule

module clock (
  input  RUN,
  input  HALT,
  output OUT
);

  wire clock_1_out, xor_1_out;

  Clock clock_1 (.out(clock_1_out));
  D_Flip_Flop #(.trigger("high")) d_ff_1 (
    .clk(1'b1), .D(clock_1_out), .Q(OUT), .en(xor_1_out));  // open: Qn, preset, reset
  xor xor_1 (xor_1_out, RUN, HALT);
endmodule
