// Logisim project toy8-no-control-v0.circ as structural Verilog: 2 circuits, main circuit main
module main (
  input  PC_load,
  input  PC_inc,
  input  [1:0] ALUOp,
  input  [1:0] R_MUX,
  input  ADDR_MUX,
  input  R_en,
  input  IR_en,
  input  RAM_str,
  output [3:0] Opcode
);

  wire clock_1_out;
  wire [3:0] counter_1_q, IR_q, multiplexer_2_out;
  wire [7:0] alu_1_out_4, bit_extender_1_out, multiplexer_1_out, R_q, ram_1_data;

  alu alu_1 (.ALUOp(ALUOp), .in_2(R_q), .in_3(ram_1_data), .out_4(alu_1_out_4));
  Multiplexer #(.select(2), .width(8), .enable("false")) multiplexer_1 (
    .in0(alu_1_out_4), .in1(ram_1_data), .in2(bit_extender_1_out), .out(multiplexer_1_out), .sel(R_MUX));  // open: in3
  assign bit_extender_1_out = {{4{1'b0}}, IR_q};  // Bit_Extender bit_extender_1
  Register #(.trigger("falling")) R (.D(multiplexer_1_out), .en(R_en), .Q(R_q), .clk(clock_1_out));  // open: clr
  Register IR (.D(ram_1_data), .en(IR_en), .Q({Opcode, IR_q}), .clk(clock_1_out));  // open: clr
  Counter #(.width(4), .max('hf), .trigger("falling")) counter_1 (
    .load(PC_load), .D(IR_q), .count(PC_inc), .Q(counter_1_q), .clk(clock_1_out));  // open: carry, clr
  Multiplexer #(.width(4), .enable("false")) multiplexer_2 (
    .in0(counter_1_q), .in1(IR_q), .out(multiplexer_2_out), .sel(ADDR_MUX));
  Clock clock_1 (.out(clock_1_out));
  RAM #(.addrWidth(4), .bus("separate")) ram_1 (
    .addr(multiplexer_2_out), .din(R_q), .data(ram_1_data), .str(RAM_str), .clk(RAM_str));  // open: sel, ld, clr

  // Notes on the sheet:
  //   PC
  //   CLK
  //   RAM
endmodule

module alu (
  input  [1:0] ALUOp,
  input  [7:0] in_2,
  input  [7:0] in_3,
  output [7:0] out_4
);

  wire [7:0] adder_1_out, and_1_out, xor_1_out;

  Adder adder_1 (.a(in_2), .b(in_3), .out(adder_1_out));  // open: cin, cout
  assign and_1_out = in_2 & in_3;  // AND_Gate and_1, 8 bits wide
  assign xor_1_out = in_2 ^ in_3;  // XOR_Gate xor_1, 8 bits wide
  Multiplexer #(.select(2), .width(8), .enable("false")) multiplexer_1 (
    .in0(adder_1_out), .in1(and_1_out), .in2(xor_1_out), .out(out_4), .sel(ALUOp));  // open: in3

  // Notes on the sheet:
  //   A
  //   B
  //   R
endmodule
